# Fritzing sketch sim808 (saved by Fritzing 0.9.3b)
breadboards: 1

parts:
  LED1 = LED - 5mm [color="Red (633nm)" package="5 mm [THT]"]
  LED2 = LED - 5mm [color="Red (633nm)" package="5 mm [THT]"]
  S1 = Pushbutton [package="[THT]"]
  S2 = Pushbutton [package="[THT]"]
  R1 = Resistor [tolerance=±5% resistance=220 package=THT]
  R2 = Resistor [tolerance=±5% resistance=220 package=THT]
  R3 = Resistor [tolerance=±5% resistance=220 package=THT]
  R4 = Resistor [tolerance=±5% resistance=220 package=THT]
  GPS2 = Adafruit Ultimate GPS Breakout
  WF1 = chipKIT WF32 [package=WF32]
  U1 = LIPO-2000mAh [package=lipo-2000]

nets (from the breadboard view):
  N1: LED1.anode, R2.Pin_1
  N2: LED2.cathode, WF1.D3
  N3: LED2.anode, R1.Pin_1
  N4: S1.Pin_1, S1.Pin_2, R3.Pin_0
  GND: S1.Pin_3, S1.Pin_4, S2.Pin_3, S2.Pin_4, R3.Pin_1, R4.Pin_1, GPS2.GND, WF1.GND, WF1.D4, WF1.D30, U1.-
  N5: S2.Pin_1, S2.Pin_2, R4.Pin_0
  N6: R1.Pin_0, R2.Pin_0, GPS2.3.3V
  N7: GPS2.TX, WF1.D39
  N8: GPS2.RX, WF1.D40
